// Digital circuit Lab02.dig as structural Verilog
module Lab02 (
  input  B,
  input  C,
  input  A,
  input  D,
  output Fa,
  output Fb,
  output Fc,
  output Fd,
  output Fe,
  output Fg,
  output Ff
);

  wire A_t, and_1_out, and_2_out, and_3_out, and_4_out, and_5_out, and_6_out, and_7_out, and_8_out,
       and_9_out, and_10_out, and_11_out, and_12_out, and_13_out, and_14_out, and_15_out, and_16_out,
       and_17_out, and_18_out, and_19_out, and_20_out, and_21_out, and_22_out, and_23_out, and_24_out,
       and_25_out, and_26_out, and_27_out, and_28_out, and_29_out, and_30_out, and_31_out, and_32_out, B_t,
       C_t, D_t;

  not not_1 (A_t, A);
  not not_2 (B_t, B);
  not not_3 (C_t, C);
  not not_4 (D_t, D);
  Seven_Seg seven_seg_1 (.a(Fa), .b(Fb), .c(Fc), .d(Fd), .e(Fe), .f(Ff), .g(Fg), .dp(1'b0));
  and and_1 (and_1_out, B_t, D_t);
  and and_2 (and_2_out, B, C);
  and and_3 (and_3_out, C, A_t);
  and and_4 (and_4_out, A_t, B, D);
  and and_5 (and_5_out, A, B_t, C_t);
  and and_6 (and_6_out, D_t, B_t);
  and and_7 (and_7_out, B_t, A_t);
  and and_8 (and_8_out, A_t, C, D);
  and and_9 (and_9_out, D, A, C_t);
  and and_10 (and_10_out, C_t, A_t, D_t);
  and and_11 (and_11_out, A, B);
  and and_12 (and_12_out, A, C);
  and and_13 (and_13_out, C, D_t);
  and and_14 (and_14_out, B_t, D_t);
  or or_1 (Fa, and_1_out, and_2_out, and_3_out, and_4_out, and_5_out);
  or or_2 (Fb, and_6_out, and_7_out, and_8_out, and_9_out, and_10_out);
  and and_15 (and_15_out, A, B_t);
  and and_16 (and_16_out, A_t, B);
  and and_17 (and_17_out, B_t, D);
  and and_18 (and_18_out, C_t, D);
  and and_19 (and_19_out, B_t, C_t);
  and and_20 (and_20_out, A, C);
  and and_21 (and_21_out, A, B_t);
  and and_22 (and_22_out, A_t, B, C_t);
  and and_23 (and_23_out, A_t, B, D_t);
  and and_24 (and_24_out, A_t, C_t, D_t);
  and and_25 (and_25_out, B, C_t);
  and and_26 (and_26_out, B, D_t);
  and and_27 (and_27_out, B_t, C);
  and and_28 (and_28_out, A, C_t);
  and and_29 (and_29_out, B, C, D_t);
  and and_30 (and_30_out, B, C_t, D);
  and and_31 (and_31_out, B_t, C, D);
  and and_32 (and_32_out, A_t, B_t, D_t);
  or or_3 (Fe, and_11_out, and_12_out, and_13_out, and_14_out);
  or or_4 (Fc, and_15_out, and_16_out, and_17_out, and_18_out, and_19_out);
  or or_5 (Ff, and_20_out, and_21_out, and_22_out, and_23_out, and_24_out);
  or or_6 (Fg, A, and_25_out, and_26_out, and_27_out);
  or or_7 (Fd, and_28_out, and_29_out, and_30_out, and_31_out, and_32_out);

  // Other names for the same wires on the sheet: FaOUT = Fa; FbOUT = Fb; FcOUT = Fc; FdOUT = Fd; FeOUT = Fe;
  //   FfOUT = Ff; FgOUT = Fg
endmodule
